# Fritzing sketch wall-e (saved by Fritzing 0.9.2b)

parts:
  Part1 = Arduino Uno (Rev3)
  M2 = DC Motor
  U1 = L298 [package=multiwatt15]
  M1 = DC Motor
  J1 = Basic Servo
  VCC2 = Battery block 9V
  VCC1 = Battery block 9V  # not connected
  HC-SR04 = SIP - 4 pins [chip_label=IC package="SIP (Single Inline) [THT]"]

nets:
  N1: Part1.D8, J1.pulse
  N2: Part1.D9_PWM, U1.IN1
  N3: Part1.D10_PWM/SS, U1.IN2
  N4: Part1.D11_PWM/MOSI, U1.IN3
  N5: Part1.D12/MISO, U1.IN4
  GND: Part1.GND, U1.GND, J1.gnd, VCC2.-, HC-SR04.Gnd
  N6: Part1.D4, HC-SR04.Echo
  N7: Part1.D5_PWM, HC-SR04.Trig
  VCC: Part1.5V, J1.vcc, HC-SR04.Vcc
  N8: M2.pin_1, U1.OUT2
  N9: M2.pin_2, U1.OUT1
  N10: U1.VLS, VCC2.+
  N11: U1.OUT3, M1.pin_2
  N12: U1.OUT4, M1.pin_1

custom parts:
  SIP - 4 pins: A SIP stand-in part for whatever you want. With 4 pins on a 300 mil single inline package (SIP) footprint.
